# Fritzing sketch file 39 (saved by Fritzing 0.9.4)
breadboards: 1

parts:
  M1 = fc-51 [package=THT]
  Part1 = Arduino Uno (Rev3)
  LED1 = LED - 5mm [color="Red (633nm)" package="5 mm [THT]"]

nets:
  N1: M1.pin1, Part1.A0
  N2: M1.pin2, Part1.GND, LED1.cathode
  N3: M1.pin3, Part1.5V
  N4: Part1.D2, LED1.anode
