# Fritzing sketch file 40,41 (saved by Fritzing 0.9.4)
breadboards: 1

parts:
  Mod1 = MQ-7 breakout
  LED1 = LED - 5mm [color="Red (633nm)" package="5 mm [THT]"]
  Part1 = Arduino Uno (Rev3)

nets:
  VCC: Mod1.VCC, Part1.5V
  GND: Mod1.GND, LED1.cathode, Part1.GND
  N1: Mod1.DO, Part1.D8
  N2: Mod1.AO, Part1.A0
  N3: LED1.anode, Part1.D2

custom parts:
  MQ-7 breakout: MQ-5 gas sensor
