# Fritzing sketch file 42 (saved by Fritzing 0.9.4)
breadboards: 1

parts:
  LED1 = LED - 5mm [color="Red (633nm)" package="5 mm [THT]"]
  S1 = Pushbutton [package="[THT]"]
  Part1 = Arduino Uno (Rev3)
  R1 = Resistor [tolerance=±5% resistance=220 package=THT]

nets:
  N1: LED1.cathode, R1.Pin_1
  N2: LED1.anode, Part1.D13/SCK
  N3: S1.Pin_1, S1.Pin_2, Part1.D2
  N4: S1.Pin_3, S1.Pin_4, Part1.GND, R1.Pin_0
